# Fritzing sketch burn_bootloader (saved by Fritzing 0.9.2b)

parts:
  Part1 = Arduino Pro Mini v13
  Part2 = Arduino Uno (Rev3) - ICSP

nets:
  VCC: Part1.VCC, Part2.5V
  GND: Part1.GND, Part2.GND
  N1: Part1.D13/SCK, Part2.D13/SCK
  N2: Part1.D12/MISO, Part2.D12/MISO
  N3: Part1.D11_PWM/MOSI, Part2.D11_PWM/MOSI
  N4: Part1.RESET, Part2.D10_PWM/SS
